// Logisim project CombinationalExamples.circ as structural Verilog
// Example1
module Example_1 (
  input  A,
  input  B,
  input  C,
  output Y
);

  wire and_1_out, nand_1_out;

  nand nand_1 (nand_1_out, A, B);
  and and_1 (and_1_out, C, A);
  or or_1 (Y, nand_1_out, and_1_out);

  // Notes on the sheet:
  //   Y = ~(AB) + AC
endmodule

module Example0 (
  input  in_1,
  input  in_2,
  input  in_3,
  input  in_4,
  input  in_5,
  input  in_6,
  output out_7,
  output out_8
);

  wire and_1_out;

  and and_1 (and_1_out, in_1, in_3);
  and and_2 (out_8, and_1_out, in_5);
  and and_3 (out_7, in_2, in_4, in_6);
endmodule

module HalfAdder (
  input  A,
  input  B,
  output Sum,
  output Carry
);

  xor xor_1 (Sum, A, B);
  and and_1 (Carry, B, A);
endmodule

module HalfAdder2 (
  input  A,
  input  B,
  output Sum,
  output Carry
);

  wire and_2_out, and_3_out, not_1_out, not_2_out;

  not not_1 (not_1_out, A);
  not not_2 (not_2_out, B);
  and and_1 (Carry, B, A);
  and and_2 (and_2_out, not_1_out, B);
  and and_3 (and_3_out, not_2_out, A);
  or or_1 (Sum, and_2_out, and_3_out);
endmodule

module XOR (
  input  A,
  input  B,
  output Sum
);

  wire and_1_out, and_2_out, not_1_out, not_2_out;

  not not_1 (not_1_out, A);
  not not_2 (not_2_out, B);
  and and_1 (and_1_out, not_1_out, B);
  and and_2 (and_2_out, not_2_out, A);
  or or_1 (Sum, and_1_out, and_2_out);
endmodule

module OR_with_NAND (
  input  in_1,
  input  in_2,
  output out_3
);

  wire nand_1_out, nand_2_out;

  nand nand_1 (nand_1_out, in_1, in_1);
  nand nand_2 (nand_2_out, in_2, in_2);
  nand nand_3 (out_3, nand_1_out, nand_2_out);
endmodule

module HalfAdder3 (
  input  A,
  input  B,
  output Sum,
  output Carry
);

  wire not_1_out, or_1_out;

  or or_1 (or_1_out, A, B);
  not not_1 (not_1_out, Carry);
  and and_1 (Carry, A, B);
  and and_2 (Sum, or_1_out, not_1_out);
endmodule

module FullAdder (
  input  C,
  input  A,
  input  B,
  output Sum,
  output Carry
);

  wire halfadder3_1_carry, halfadder3_2_carry, halfadder3_2_sum;

  HalfAdder3 halfadder3_1 (.A(C), .B(halfadder3_2_sum), .Sum(Sum), .Carry(halfadder3_1_carry));
  HalfAdder3 halfadder3_2 (.A(A), .B(B), .Sum(halfadder3_2_sum), .Carry(halfadder3_2_carry));
  or or_1 (Carry, halfadder3_1_carry, halfadder3_2_carry);
endmodule

module FullAdder2 (
  input  A,
  input  B,
  input  C,
  output Sum,
  output Carry
);

  wire and_1_out, and_2_out, and_3_out, and_4_out, and_5_out, not_1_out, or_1_out;

  and and_1 (and_1_out, C, B, A);
  or or_1 (or_1_out, C, B, A);
  and and_2 (and_2_out, C, B);
  and and_3 (and_3_out, C, A);
  and and_4 (and_4_out, B, A);
  or or_2 (Carry, and_2_out, and_3_out, and_4_out);
  not not_1 (not_1_out, Carry);
  and and_5 (and_5_out, or_1_out, not_1_out);
  or or_3 (Sum, and_1_out, and_5_out);
endmodule

module Adder (
  input  A0,
  input  B0,
  input  A1,
  input  B1,
  input  A2,
  input  B2,
  input  A3,
  input  B3,
  output S0,
  output S1,
  output S2,
  output S3
);

  wire fulladder_1_carry, fulladder_2_carry, halfadder3_1_carry;

  HalfAdder3 halfadder3_1 (.A(A0), .B(B0), .Sum(S0), .Carry(halfadder3_1_carry));
  FullAdder fulladder_1 (.C(halfadder3_1_carry), .A(A1), .B(B1), .Sum(S1), .Carry(fulladder_1_carry));
  FullAdder fulladder_2 (.C(fulladder_1_carry), .A(A2), .B(B2), .Sum(S2), .Carry(fulladder_2_carry));
  FullAdder fulladder_3 (.C(fulladder_2_carry), .A(A3), .B(B3), .Sum(S3));  // open: Carry
endmodule

module L_4BitAdder (
  input  Cin,
  input  A0,
  input  A1,
  input  A2,
  input  A3,
  input  B0,
  input  B1,
  input  B2,
  input  B3,
  output S0,
  output S1,
  output S2,
  output S3,
  output Cout
);

  wire fulladder_1_carry, fulladder_2_carry, fulladder_3_carry;

  FullAdder fulladder_1 (.C(Cin), .A(A0), .B(B0), .Sum(S0), .Carry(fulladder_1_carry));
  FullAdder fulladder_2 (.C(fulladder_1_carry), .A(A1), .B(B1), .Sum(S1), .Carry(fulladder_2_carry));
  FullAdder fulladder_3 (.C(fulladder_2_carry), .A(A2), .B(B2), .Sum(S2), .Carry(fulladder_3_carry));
  FullAdder fulladder_4 (.C(fulladder_3_carry), .A(A3), .B(B3), .Sum(S3), .Carry(Cout));
endmodule

module ALU (
  input  SUB,
  input  [3:0] A,
  input  [3:0] B,
  output Zero,
  output [3:0] R,
  output Carry_Out,
  output overflow,
  output [3:0] out_8,
  output [3:0] out_9
);

  wire and_2_out, and_3_out;
  wire [3:0] l_4bitxor_1_out_3;

  // Probe on A
  // Probe on B
  L_4BitXor l_4bitxor_1 (.in_1(SUB), .in_2(B), .out_3(l_4bitxor_1_out_3));
  assign out_8 = A & B;  // AND_Gate and_1, 4 bits wide
  assign out_9 = A | B;  // OR_Gate or_1, 4 bits wide
  L_4BitAdder l_4bitadder_1 (
    .Cin(SUB), .A0(A[0]), .A1(A[1]), .A2(A[2]), .A3(A[3]), .B0(l_4bitxor_1_out_3[0]),
    .B1(l_4bitxor_1_out_3[1]), .B2(l_4bitxor_1_out_3[2]), .B3(l_4bitxor_1_out_3[3]), .S0(R[0]), .S1(R[1]),
    .S2(R[2]), .S3(R[3]), .Cout(Carry_Out));
  nand nand_1 (Zero, R[3], R[2], R[1], R[0]);
  and and_2 (and_2_out, ~A[3], ~l_4bitxor_1_out_3[3], R[3]);  // AND_Gate
  and and_3 (and_3_out, A[3], l_4bitxor_1_out_3[3], ~R[3]);  // AND_Gate
  // Probe on R
  or or_2 (overflow, and_2_out, and_3_out);
endmodule

module L_4BitXor (
  input  in_1,
  input  [3:0] in_2,
  output [3:0] out_3
);

  xor xor_1 (out_3[0], in_1, in_2[0]);
  xor xor_2 (out_3[1], in_2[1], in_1);
  xor xor_3 (out_3[2], in_2[2], in_1);
  xor xor_4 (out_3[3], in_2[3], in_1);
endmodule

module Multiplexors (
  input  [7:0] D,
  input  [7:0] D_2,
  input  H,
  input  G,
  input  F,
  input  E,
  input  D_3,
  input  C,
  input  B,
  input  A,
  input  S0,
  input  S1,
  input  [2:0] S2,
  input  [2:0] S2_2,
  input  S2_3,
  input  H_2,
  input  G_2,
  input  F_2,
  input  E_2,
  input  D_4,
  input  C_2,
  input  B_2,
  input  A_2,
  input  H_3,
  input  G_3,
  input  F_3,
  input  E_3,
  input  D_5,
  input  C_3,
  input  B_3,
  input  A_3,
  input  S2_4,
  input  S1_2,
  input  S0_2,
  input  [2:0] S2_5,
  output OUT,
  output OUT_2,
  output OUT_3,
  output OUT_4,
  output OUT_5
);

  wire and_1_out, and_2_out, and_3_out, and_4_out, and_5_out, and_6_out, and_7_out, and_8_out, and_9_out,
       and_10_out, and_11_out, and_12_out, and_13_out, and_14_out, and_15_out, and_16_out, and_17_out,
       and_18_out, and_19_out, and_20_out, and_21_out, and_22_out, and_23_out, and_24_out, decoder_1_out0,
       decoder_1_out1, decoder_1_out2, decoder_1_out3, decoder_1_out4, decoder_1_out5, decoder_1_out6,
       decoder_1_out7, decoder_2_out0, decoder_2_out1, decoder_2_out2, decoder_2_out3, decoder_2_out4,
       decoder_2_out5, decoder_2_out6, decoder_2_out7, decoder_3_out0, decoder_3_out1, decoder_3_out2,
       decoder_3_out3, decoder_3_out4, decoder_3_out5, decoder_3_out6, decoder_3_out7, decoder_4_out0,
       decoder_4_out1, decoder_4_out2, decoder_4_out3, decoder_4_out4, decoder_4_out5, decoder_4_out6,
       decoder_4_out7, decoder_5_out0, decoder_5_out1, decoder_5_out2, decoder_5_out3, decoder_5_out4,
       decoder_5_out5, decoder_5_out6, decoder_5_out7, or_1_out, or_2_out, or_3_out, or_5_out, or_7_out,
       or_8_out;

  Decoder_part #(.select(3), .enable("false")) decoder_1 (
    .out0(decoder_1_out0), .out1(decoder_1_out1), .out2(decoder_1_out2), .out3(decoder_1_out3),
    .out4(decoder_1_out4), .out5(decoder_1_out5), .out6(decoder_1_out6), .out7(decoder_1_out7),
    .sel({S2_3, S1, S0}));
  Decoder_part #(.select(3), .enable("false")) decoder_2 (
    .out0(decoder_2_out0), .out1(decoder_2_out1), .out2(decoder_2_out2), .out3(decoder_2_out3),
    .out4(decoder_2_out4), .out5(decoder_2_out5), .out6(decoder_2_out6), .out7(decoder_2_out7),
    .sel({S0_2, S1_2, S2_4}));
  and and_1 (and_1_out, decoder_1_out7, H);
  and and_2 (and_2_out, decoder_2_out7, H_2);
  or or_1 (or_1_out, and_2_out, and_6_out);
  and and_3 (and_3_out, decoder_1_out6, G);
  and and_4 (and_4_out, decoder_1_out5, F);
  and and_5 (and_5_out, decoder_2_out5, F_2);
  and and_6 (and_6_out, decoder_2_out6, G_2);
  or or_2 (or_2_out, and_5_out, and_9_out);
  or or_3 (or_3_out, or_1_out, or_2_out);
  and and_7 (and_7_out, decoder_1_out4, E);
  and and_8 (and_8_out, decoder_1_out3, D_3);
  or or_4 (OUT, and_1_out, and_3_out, and_4_out, and_7_out, and_8_out, and_11_out, and_12_out, and_15_out);
  and and_9 (and_9_out, decoder_2_out4, E_2);
  and and_10 (and_10_out, decoder_2_out3, D_4);
  or or_5 (or_5_out, and_10_out, and_13_out);
  or or_6 (OUT_4, or_3_out, or_8_out);
  and and_11 (and_11_out, decoder_1_out2, C);
  and and_12 (and_12_out, decoder_1_out1, B);
  and and_13 (and_13_out, decoder_2_out2, C_2);
  and and_14 (and_14_out, decoder_2_out1, B_2);
  or or_7 (or_7_out, and_14_out, and_16_out);
  or or_8 (or_8_out, or_5_out, or_7_out);
  and and_15 (and_15_out, decoder_1_out0, A);
  and and_16 (and_16_out, decoder_2_out0, A_2);
  Decoder_part #(.select(3), .enable("false")) decoder_3 (
    .out0(decoder_3_out0), .out1(decoder_3_out1), .out2(decoder_3_out2), .out3(decoder_3_out3),
    .out4(decoder_3_out4), .out5(decoder_3_out5), .out6(decoder_3_out6), .out7(decoder_3_out7), .sel(S2));
  and and_17 (and_17_out, decoder_3_out7, D[7]);
  Decoder_part #(.select(3), .enable("false")) decoder_4 (
    .out0(decoder_4_out0), .out1(decoder_4_out1), .out2(decoder_4_out2), .out3(decoder_4_out3),
    .out4(decoder_4_out4), .out5(decoder_4_out5), .out6(decoder_4_out6), .out7(decoder_4_out7), .sel(S2_5));
  and and_18 (and_18_out, decoder_3_out5, D[5]);
  and and_19 (and_19_out, decoder_3_out6, D[6]);
  assign OUT_5 = decoder_4_out7 ? H_3 : 1'bz;  // Controlled_Buffer controlled_buffer_1
  assign OUT_5 = decoder_4_out6 ? G_3 : 1'bz;  // Controlled_Buffer controlled_buffer_2
  and and_20 (and_20_out, decoder_3_out3, D[3]);
  and and_21 (and_21_out, decoder_3_out4, D[4]);
  or or_9 (OUT_2, and_17_out, and_19_out, and_18_out, and_21_out, and_20_out, and_23_out, and_22_out, and_24_out);
  assign OUT_5 = decoder_4_out4 ? E_3 : 1'bz;  // Controlled_Buffer controlled_buffer_3
  assign OUT_5 = decoder_4_out5 ? F_3 : 1'bz;  // Controlled_Buffer controlled_buffer_4
  and and_22 (and_22_out, decoder_3_out1, D[1]);
  and and_23 (and_23_out, decoder_3_out2, D[2]);
  assign OUT_5 = decoder_4_out2 ? C_3 : 1'bz;  // Controlled_Buffer controlled_buffer_5
  assign OUT_5 = decoder_4_out3 ? D_5 : 1'bz;  // Controlled_Buffer controlled_buffer_6
  and and_24 (and_24_out, decoder_3_out0, D[0]);
  assign OUT_5 = decoder_4_out0 ? A_3 : 1'bz;  // Controlled_Buffer controlled_buffer_7
  assign OUT_5 = decoder_4_out1 ? B_3 : 1'bz;  // Controlled_Buffer controlled_buffer_8
  Decoder_part #(.select(3), .enable("false")) decoder_5 (
    .out0(decoder_5_out0), .out1(decoder_5_out1), .out2(decoder_5_out2), .out3(decoder_5_out3),
    .out4(decoder_5_out4), .out5(decoder_5_out5), .out6(decoder_5_out6), .out7(decoder_5_out7), .sel(S2_2));
  assign OUT_3 = decoder_5_out7 ? D_2[7] : 1'bz;  // Controlled_Buffer controlled_buffer_9
  assign OUT_3 = decoder_5_out6 ? D_2[6] : 1'bz;  // Controlled_Buffer controlled_buffer_10
  assign OUT_3 = decoder_5_out5 ? D_2[5] : 1'bz;  // Controlled_Buffer controlled_buffer_11
  assign OUT_3 = decoder_5_out3 ? D_2[3] : 1'bz;  // Controlled_Buffer controlled_buffer_12
  assign OUT_3 = decoder_5_out4 ? D_2[4] : 1'bz;  // Controlled_Buffer controlled_buffer_13
  assign OUT_3 = decoder_5_out1 ? D_2[1] : 1'bz;  // Controlled_Buffer controlled_buffer_14
  assign OUT_3 = decoder_5_out2 ? D_2[2] : 1'bz;  // Controlled_Buffer controlled_buffer_15
  assign OUT_3 = decoder_5_out0 ? D_2[0] : 1'bz;  // Controlled_Buffer controlled_buffer_16
endmodule

module Decoder (
  input  S0,
  input  S1,
  input  S2,
  output out_4,
  output out_5,
  output out_6,
  output out_7,
  output out_8,
  output out_9,
  output out_10,
  output out_11
);

  and and_1 (out_4, ~S2, ~S1, ~S0);  // AND_Gate
  and and_2 (out_5, ~S2, ~S1, S0);  // AND_Gate
  and and_3 (out_6, ~S2, S1, ~S0);  // AND_Gate
  and and_4 (out_7, ~S2, S1, S0);  // AND_Gate
  and and_5 (out_8, S2, ~S1, ~S0);  // AND_Gate
  and and_6 (out_9, S2, ~S1, S0);  // AND_Gate
  and and_7 (out_10, S2, S1, ~S0);  // AND_Gate
  and and_8 (out_11, S2, S1, S0);
endmodule
