// Logisim project KITT.circ as structural Verilog: 1 circuit, main circuit KITT
module KITT (
);

  wire and_1_out, and_2_out, and_3_out, and_4_out, and_5_out, and_6_out, and_7_out, and_8_out, and_9_out,
       and_10_out, and_11_out, and_12_out, and_13_out, and_14_out, and_15_out, and_16_out, clock_1_out,
       d_ff_1_q, d_ff_1_qn, d_ff_2_q, d_ff_2_qn, d_ff_3_q, d_ff_3_qn, d_ff_4_q, d_ff_4_qn, or_1_out,
       or_2_out, or_3_out, or_4_out, or_5_out, or_6_out, or_7_out, or_8_out;

  or or_1 (or_1_out, and_1_out, and_2_out);
  and and_1 (and_1_out, d_ff_1_qn, d_ff_2_qn, d_ff_3_qn, d_ff_4_qn);
  and and_2 (and_2_out, d_ff_1_q, d_ff_2_q, d_ff_3_q, d_ff_4_q);
  Clock clock_1 (.out(clock_1_out));
  LED led_1 (.in(or_1_out));
  LED led_2 (.in(or_2_out));
  or or_2 (or_2_out, and_4_out, and_3_out);
  and and_3 (and_3_out, d_ff_1_qn, d_ff_2_q, d_ff_3_q, d_ff_4_q);
  and and_4 (and_4_out, d_ff_1_q, d_ff_2_qn, d_ff_3_qn, d_ff_4_qn);
  D_Flip_Flop d_ff_1 (.D(d_ff_1_qn), .clk(clock_1_out), .Q(d_ff_1_q), .Qn(d_ff_1_qn));  // open: preset, reset
  LED led_3 (.in(or_4_out));
  LED led_4 (.in(or_6_out));
  LED led_5 (.in(or_5_out));
  LED led_6 (.in(or_3_out));
  or or_3 (or_3_out, and_5_out, and_6_out);
  and and_5 (and_5_out, d_ff_1_qn, d_ff_2_q, d_ff_3_qn, d_ff_4_qn);
  D_Flip_Flop d_ff_2 (.D(d_ff_2_qn), .clk(d_ff_1_qn), .Q(d_ff_2_q), .Qn(d_ff_2_qn));  // open: preset, reset
  LED led_7 (.in(or_7_out));
  LED led_8 (.in(or_8_out));
  and and_6 (and_6_out, d_ff_1_q, d_ff_2_qn, d_ff_3_q, d_ff_4_q);
  and and_7 (and_7_out, d_ff_1_q, d_ff_2_q, d_ff_3_qn, d_ff_4_qn);
  or or_4 (or_4_out, and_7_out, and_8_out);
  and and_8 (and_8_out, d_ff_1_qn, d_ff_2_qn, d_ff_3_q, d_ff_4_q);
  D_Flip_Flop d_ff_3 (.D(d_ff_3_qn), .clk(d_ff_2_qn), .Q(d_ff_3_q), .Qn(d_ff_3_qn));  // open: preset, reset
  or or_5 (or_5_out, and_9_out, and_10_out);
  and and_9 (and_9_out, d_ff_1_qn, d_ff_2_qn, d_ff_3_q, d_ff_4_qn);
  D_Flip_Flop d_ff_4 (.D(d_ff_4_qn), .clk(d_ff_3_qn), .Q(d_ff_4_q), .Qn(d_ff_4_qn));  // open: preset, reset
  and and_10 (and_10_out, d_ff_1_q, d_ff_2_q, d_ff_3_qn, d_ff_4_q);
  and and_11 (and_11_out, d_ff_1_q, d_ff_2_qn, d_ff_3_q, d_ff_4_qn);
  or or_6 (or_6_out, and_11_out, and_12_out);
  and and_12 (and_12_out, d_ff_1_qn, d_ff_2_q, d_ff_3_qn, d_ff_4_q);
  or or_7 (or_7_out, and_13_out, and_14_out);
  and and_13 (and_13_out, d_ff_1_qn, d_ff_2_q, d_ff_3_q, d_ff_4_qn);
  and and_14 (and_14_out, d_ff_1_q, d_ff_2_qn, d_ff_3_qn, d_ff_4_q);
  and and_15 (and_15_out, d_ff_1_q, d_ff_2_q, d_ff_3_q, d_ff_4_qn);
  or or_8 (or_8_out, and_15_out, and_16_out);
  and and_16 (and_16_out, d_ff_1_qn, d_ff_2_qn, d_ff_3_qn, d_ff_4_q);

  // Notes on the sheet:
  //   1
  //   Alisa GAGINA, 260770497
  //   2
  //   A
  //   Enable ticks at a frequency of 32 Hz
  //   3
  //   B
  //   4
  //   C
  //   5
  //   D
  //   6
  //   7
  //   8
  //   ex. 8 turns on @ 1110 or 0001
  //   ABCD -> 0000
  //   D'
  //   D
  //   C'
  //   C
  //   B'
  //   B
  //   A'
  //   A
endmodule
