// Logisim project SequentialDivider.circ as structural Verilog: 10 circuits, main circuit Divider
module Divider (
  input  in_1,
  input  RESET,
  input  [3:0] in_3,
  output out_4,
  output [7:0] out_5
);

  wire and_1_out, and_2_out, clock_1_out, not_1_out, not_2_out, or_1_out, undriven, undriven_2, undriven_3;
  wire [7:0] multiplexer_1_out, undriven_4;

  // Probe on undriven
  not not_1 (not_1_out, in_1);
  and and_1 (and_1_out, and_2_out, not_2_out);
  and and_2 (and_2_out, not_1_out, clock_1_out);
  Clock clock_1 (.out(clock_1_out));
  Counter #(.width(1), .max('h1), .ongoal("load")) counter_1 (
    .clr(in_1), .up(1'b1), .clk(and_1_out), .D(1'b0), .carry(out_4));  // open: load, count, Q
  not not_2 (not_2_out, out_4);
  // Probe on undriven_3
  // Probe on in_3
  Multiplexer #(.width(8)) multiplexer_1 (
    .in1(undriven_4), .out(multiplexer_1_out), .sel(or_1_out), .en(undriven_2));  // open: in0
  // Probe on undriven_4
  or or_1 (or_1_out, in_1, clock_1_out);
  // Probe on out_5

  // Notes on the sheet:
  //   First name LAST NAME, Student Number
endmodule

module control (
  input  RESET,
  input  neg,
  output loaddivisor,
  output loaddivident,
  output writesubintor,
  output shiftinneg,
  output shiftq,
  output shiftr,
  output DONE
);

  wire clock_1_out, counter_1_carry, d_ff_1_q, d_ff_2_q, d_ff_3_q, d_ff_4_q, outp_1_counterup, undriven,
       undriven_2, undriven_3, undriven_4;

  Clock clock_1 (.out(clock_1_out));
  D_Flip_Flop d_ff_1 (.D(undriven_3), .Q(d_ff_1_q));  // open: clk, Qn, preset, reset
  D_Flip_Flop d_ff_2 (.D(undriven_4), .Q(d_ff_2_q));  // open: clk, Qn, preset, reset
  D_Flip_Flop d_ff_3 (.D(undriven_2), .Q(d_ff_3_q));  // open: clk, Qn, preset, reset
  D_Flip_Flop d_ff_4 (.D(undriven), .Q(d_ff_4_q));  // open: clk, Qn, preset, reset
  NextS nexts_1 (
    .reset(RESET), .s0in(undriven_3), .s1in(undriven_4), .s2in(undriven_2), .s3in(undriven),
    .countercarry(counter_1_carry), .so(d_ff_1_q), .s1(d_ff_2_q), .s2(d_ff_3_q), .s3(d_ff_4_q));
  Counter #(.width(4), .max('h4)) counter_1 (
    .up(outp_1_counterup), .clk(clock_1_out), .carry(counter_1_carry));  // open: clr, load, count, D, Q
  Outp outp_1 (
    .s0(d_ff_1_q), .neg(neg), .s1(d_ff_2_q), .s2(d_ff_3_q), .countcarry(counter_1_carry), .s3(d_ff_4_q),
    .loaddivisor(loaddivisor), .loaddivident(loaddivident), .loadsub(writesubintor), .shiftin(shiftinneg),
    .counterup(outp_1_counterup), .shiftq(shiftq), .shiftr(shiftr), .done(DONE));
endmodule

module NextS (
  input  reset,
  input  s0in,
  input  s1in,
  input  s2in,
  input  s3in,
  input  countercarry,
  output so,
  output s1,
  output s2,
  output s3
);

  wire and_1_out, and_3_out, and_4_out, and_5_out, not_1_out;

  not not_1 (not_1_out, reset);
  and and_1 (and_1_out, s0in, not_1_out);
  and and_2 (s2, s1in, not_1_out);
  and and_3 (and_3_out, s2in, not_1_out, ~countercarry);  // AND_Gate
  and and_4 (and_4_out, s3in, not_1_out);
  and and_5 (and_5_out, s2in, not_1_out, countercarry);
  or or_1 (s1, and_1_out, and_3_out);
  or or_2 (s3, and_5_out, and_4_out);

  assign so = reset;
endmodule

module Outp (
  input  s0,
  input  neg,
  input  s1,
  input  s2,
  input  countcarry,
  input  s3,
  output loaddivisor,
  output loaddivident,
  output loadsub,
  output shiftin,
  output counterup,
  output shiftq,
  output shiftr,
  output done
);

  wire not_1_out, not_2_out;

  not not_1 (not_1_out, neg);
  and and_1 (loadsub, not_1_out, s1);
  not not_2 (not_2_out, countcarry);
  and and_2 (shiftr, s2, not_2_out);

  assign counterup = s2;
  assign done = s3;
  assign loaddivident = s0;
  assign loaddivisor = s0;
  assign shiftin = loadsub;
  assign shiftq = s2;
endmodule

module DivRem (
  input  [3:0] Divident,
  input  [3:0] Sub,
  input  QShiin,
  input  WriteSub,
  input  ShiftQ,
  input  ShiftR,
  input  LoadDiv,
  input  RESET,
  output [3:0] REMAINDER,
  output [3:0] Quotient
);

  wire clock_1_out, d_ff_1_q, leftrem_1_shiout;

  Clock clock_1 (.out(clock_1_out));
  LeftRem leftrem_1 (
    .Shift(d_ff_1_q), .Load(LoadDiv), .Enable(ShiftQ), .Reset(RESET), .Shiin(Divident), .Outt(Quotient),
    .ShiOut(leftrem_1_shiout));
  D_Flip_Flop d_ff_1 (.D(QShiin), .clk(clock_1_out), .Q(d_ff_1_q));  // open: Qn, preset, reset
  LeftRem leftrem_2 (
    .Shift(leftrem_1_shiout), .Load(WriteSub), .Enable(ShiftR), .Reset(RESET), .Shiin(Sub), .Outt(REMAINDER));  // open: ShiOut
endmodule

module LeftRem (
  input  Shift,
  input  Load,
  input  Enable,
  input  Reset,
  input  [3:0] Shiin,
  output [3:0] Outt,
  output ShiOut
);

  wire clock_1_out;

  Clock clock_1 (.out(clock_1_out));
  // Shift_Register #(.length(4)) shift_register_1: pin names not known; wires that end beside it: Reset, Load, Enable, clock_1_out, Shift, Shiin[0], Shiin[1], Shiin[2], Shiin[3], Outt[3], Outt[0], Outt[1], Outt[2]

  assign ShiOut = Outt[3];
endmodule

module divisorin (
  input  [3:0] Divisor,
  input  loadin,
  input  reset,
  output [3:0] Divisorout
);

  wire clock_1_out;

  Clock clock_1 (.out(clock_1_out));
  Register #(.width(4)) register_1 (.D(Divisor), .en(loadin), .clk(clock_1_out), .Q(Divisorout), .clr(reset));
endmodule

module subtraction (
  input  [7:0] in_1,
  input  [7:0] in_2,
  input  in_3,
  input  in_4,
  output [7:0] out_5
);

  wire adder_1_cout, register_1_q;
  wire [7:0] adder_1_out, register_2_q;

  // Probe on register_2_q
  Adder adder_1 (.a(in_2), .b(register_2_q), .out(adder_1_out), .cin(register_1_q), .cout(adder_1_cout));
  Register #(.width(1)) register_1 (.D(adder_1_cout), .clk(in_3), .Q(register_1_q), .clr(in_3));  // open: en
  Multiplexer #(.width(8), .enable("false")) multiplexer_1 (
    .in0(register_2_q), .in1(adder_1_out), .out(out_5), .sel(in_3));
  Register #(.trigger("falling")) register_2 (.D(out_5), .clk(in_3), .Q(register_2_q), .clr(in_4));  // open: en
endmodule

module dividin (
  input  in_1,
  input  in_2,
  input  in_3,
  input  [3:0] in_4,
  output out_5,
  output [3:0] out_6
);

  // Shift_Register #(.length(4)) shift_register_1: pin names not known; wires that end beside it: in_1, in_2, in_3, 1'b0, in_4[0], in_4[1], in_4[2], in_4[3], out_6[0], out_6[1], out_6[2], out_5

  assign out_6[3] = out_5;
endmodule

module Divisin (
  input  in_1,
  input  in_2,
  input  in_3,
  input  [3:0] in_4,
  output [7:0] out_5
);

  wire [7:0] bit_extender_1_out;

  assign bit_extender_1_out = {{4{in_4[3]}}, in_4};  // Bit_Extender bit_extender_1
  // Shift_Register shift_register_1: pin names not known; wires that end beside it: in_1, in_2, in_3, 1'b0, bit_extender_1_out[0], bit_extender_1_out[1], bit_extender_1_out[2], bit_extender_1_out[3], bit_extender_1_out[4], bit_extender_1_out[5], bit_extender_1_out[6], bit_extender_1_out[7], out_5[0], out_5[1], out_5[2], out_5[3], out_5[4], out_5[5], out_5[6], out_5[7]
endmodule
