// Logisim project SequentialExamples.circ as structural Verilog
module RS_Unclocked (
  input  R,
  input  S,
  output Q,
  output QNOT
);

  nor nor_1 (Q, R, QNOT);
  nor nor_2 (QNOT, Q, S);
endmodule

module RS_Clocked (
  input  R,
  input  C,
  input  S,
  output Q,
  output QNOT
);

  wire and_1_out, and_2_out;

  and and_1 (and_1_out, R, C);
  and and_2 (and_2_out, C, S);
  nor nor_1 (Q, and_1_out, QNOT);
  nor nor_2 (QNOT, Q, and_2_out);
endmodule

module D_Latch (
  input  C,
  input  D,
  output Q,
  output QNOT
);

  wire and_1_out, and_2_out, not_1_out;

  not not_1 (not_1_out, D);
  and and_1 (and_1_out, C, not_1_out);
  and and_2 (and_2_out, C, D);
  nor nor_1 (Q, and_1_out, QNOT);
  nor nor_2 (QNOT, Q, and_2_out);
endmodule

module D_Flip_Flop (
  input  C,
  input  D,
  output Q,
  output QNOT
);

  wire d_latch_1_q, not_1_out;

  not not_1 (not_1_out, C);
  D_Latch d_latch_1 (.C(C), .D(D), .Q(d_latch_1_q));  // open: QNOT
  D_Latch d_latch_2 (.C(not_1_out), .D(d_latch_1_q), .Q(Q), .QNOT(QNOT));

  // Notes on the sheet:
  //   Falling Edge Triggered D Flip Flop
endmodule

module Toggle_FF (
  input  C,
  output Q
);

  wire d_ff_1_qn;

  D_Flip_Flop_part d_ff_1 (.D(d_ff_1_qn), .clk(C), .Q(Q), .Qn(d_ff_1_qn));  // open: preset, reset
endmodule

module Count_Register (
  input  in_1,
  input  in_2,
  input  in_3,
  input  in_4,
  input  in_5,
  output Q3,
  output Q2,
  output Q1,
  output Q0,
  output out_10,
  output out_11,
  output out_12,
  output out_13,
  output out_14,
  output out_15,
  output out_16,
  output out_17,
  output out_18,
  output out_19,
  output out_20,
  output out_21,
  output out_22,
  output out_23,
  output out_24,
  output out_25
);

  wire d_ff_1_qn, d_ff_2_qn, d_ff_3_qn, d_ff_4_qn, d_ff_5_qn, d_ff_6_qn, d_ff_7_qn, d_ff_8_qn, d_ff_9_qn,
       d_ff_10_qn, d_ff_11_qn, d_ff_12_qn, d_ff_13_qn, d_ff_14_qn, d_ff_15_qn, d_ff_16_qn, d_ff_17_qn,
       d_ff_18_qn, d_ff_19_qn, d_ff_20_qn;

  D_Flip_Flop_part d_ff_1 (.D(d_ff_1_qn), .clk(d_ff_7_qn), .Q(out_10), .Qn(d_ff_1_qn));  // open: preset, reset
  D_Flip_Flop_part #(.trigger("falling")) d_ff_2 (
    .D(d_ff_2_qn), .clk(out_15), .Q(out_14), .Qn(d_ff_2_qn));  // open: preset, reset
  D_Flip_Flop_part d_ff_3 (.D(d_ff_3_qn), .clk(out_19), .Q(out_18), .Qn(d_ff_3_qn));  // open: preset, reset
  D_Flip_Flop_part d_ff_4 (.D(d_ff_4_qn), .clk(out_23), .Q(out_22), .Qn(d_ff_4_qn));  // open: preset, reset
  D_Flip_Flop_part #(.trigger("falling")) d_ff_5 (
    .D(d_ff_5_qn), .clk(d_ff_6_qn), .Q(Q3), .Qn(d_ff_5_qn));  // open: preset, reset
  D_Flip_Flop_part #(.trigger("falling")) d_ff_6 (
    .D(d_ff_6_qn), .clk(d_ff_12_qn), .Q(Q2), .Qn(d_ff_6_qn));  // open: preset, reset
  D_Flip_Flop_part d_ff_7 (.D(d_ff_7_qn), .clk(d_ff_13_qn), .Q(out_11), .Qn(d_ff_7_qn));  // open: preset, reset
  D_Flip_Flop_part #(.trigger("falling")) d_ff_8 (
    .D(d_ff_8_qn), .clk(out_16), .Q(out_15), .Qn(d_ff_8_qn));  // open: preset, reset
  D_Flip_Flop_part d_ff_9 (.D(d_ff_9_qn), .clk(out_20), .Q(out_19), .Qn(d_ff_9_qn));  // open: preset, reset
  D_Flip_Flop_part d_ff_10 (.D(d_ff_10_qn), .clk(out_24), .Q(out_23), .Qn(d_ff_10_qn));  // open: preset, reset
  D_Flip_Flop_part d_ff_11 (.D(d_ff_11_qn), .clk(out_25), .Q(out_24), .Qn(d_ff_11_qn));  // open: preset, reset
  D_Flip_Flop_part #(.trigger("falling")) d_ff_12 (
    .D(d_ff_12_qn), .clk(d_ff_16_qn), .Q(Q1), .Qn(d_ff_12_qn));  // open: preset, reset
  D_Flip_Flop_part d_ff_13 (.D(d_ff_13_qn), .clk(d_ff_17_qn), .Q(out_12), .Qn(d_ff_13_qn));  // open: preset, reset
  D_Flip_Flop_part #(.trigger("falling")) d_ff_14 (
    .D(d_ff_14_qn), .clk(out_17), .Q(out_16), .Qn(d_ff_14_qn));  // open: preset, reset
  D_Flip_Flop_part d_ff_15 (.D(d_ff_15_qn), .clk(out_21), .Q(out_20), .Qn(d_ff_15_qn));  // open: preset, reset
  D_Flip_Flop_part #(.trigger("falling")) d_ff_16 (
    .D(d_ff_16_qn), .clk(in_1), .Q(Q0), .Qn(d_ff_16_qn));  // open: preset, reset
  D_Flip_Flop_part d_ff_17 (.D(d_ff_17_qn), .clk(in_2), .Q(out_13), .Qn(d_ff_17_qn));  // open: preset, reset
  D_Flip_Flop_part #(.trigger("falling")) d_ff_18 (
    .D(d_ff_18_qn), .clk(in_3), .Q(out_17), .Qn(d_ff_18_qn));  // open: preset, reset
  D_Flip_Flop_part d_ff_19 (.D(d_ff_19_qn), .clk(in_4), .Q(out_21), .Qn(d_ff_19_qn));  // open: preset, reset
  D_Flip_Flop_part d_ff_20 (.D(d_ff_20_qn), .clk(in_5), .Q(out_25), .Qn(d_ff_20_qn));  // open: preset, reset

  // Notes on the sheet:
  //   Count decreases on falling edges
  //   Count increases on rising edges
  //   Count increases on falling edges
  //   Count decreases on rising edges
  //   Count decreases on rising edges (Q instead of Q' to next bit's clock)
endmodule

module Shift_Register (
  input  Din,
  input  Clock,
  output out_3,
  output out_4,
  output out_5,
  output out_6
);

  D_Flip_Flop_part d_ff_1 (.D(Din), .clk(Clock), .Q(out_3));  // open: Qn, preset, reset
  D_Flip_Flop_part d_ff_2 (.D(out_3), .clk(Clock), .Q(out_4));  // open: Qn, preset, reset
  D_Flip_Flop_part d_ff_3 (.D(out_4), .clk(Clock), .Q(out_5));  // open: Qn, preset, reset
  D_Flip_Flop_part d_ff_4 (.D(out_5), .clk(Clock), .Q(out_6));  // open: Qn, preset, reset
endmodule

module Register (
  input  D3,
  input  D2,
  input  D1,
  input  D0,
  input  Clock,
  output Q3,
  output Q2,
  output Q1,
  output Q0
);

  D_Flip_Flop_part #(.trigger("falling")) d_ff_1 (.D(D3), .clk(Clock), .Q(Q3));  // open: Qn, preset, reset
  D_Flip_Flop_part #(.trigger("falling")) d_ff_2 (.D(D2), .clk(Clock), .Q(Q2));  // open: Qn, preset, reset
  D_Flip_Flop_part #(.trigger("falling")) d_ff_3 (.D(D1), .clk(Clock), .Q(Q1));  // open: Qn, preset, reset
  D_Flip_Flop_part #(.trigger("falling")) d_ff_4 (.D(D0), .clk(Clock), .Q(Q0));  // open: Qn, preset, reset
endmodule

module D_Latch_with_reset (
  input  R,
  input  C,
  input  D,
  output Q,
  output QNOT
);

  wire and_1_out, and_2_out, not_1_out, or_1_out;

  not not_1 (not_1_out, D);
  and and_1 (and_1_out, C, not_1_out);
  and and_2 (and_2_out, C, D);
  or or_1 (or_1_out, R, QNOT);
  nor nor_1 (Q, and_1_out, or_1_out);
  nor nor_2 (QNOT, Q, and_2_out);
endmodule

module DFF_Rising_and_Falling (
  input  C,
  input  D,
  input  C_2,
  input  D_2,
  output Q,
  output QNOT,
  output Q_RE,
  output QN_RE
);

  wire d_latch_1_q, d_latch_2_q, not_1_out, not_2_out;

  not not_1 (not_1_out, C);
  D_Latch d_latch_1 (.C(C), .D(D), .Q(d_latch_1_q));  // open: QNOT
  not not_2 (not_2_out, C_2);
  D_Latch d_latch_2 (.C(not_2_out), .D(D_2), .Q(d_latch_2_q));  // open: QNOT
  D_Latch d_latch_3 (.C(not_1_out), .D(d_latch_1_q), .Q(Q), .QNOT(QNOT));
  D_Latch d_latch_4 (.C(C_2), .D(d_latch_2_q), .Q(Q_RE), .QNOT(QN_RE));

  // Notes on the sheet:
  //   Falling Edge Triggered D Flip Flop
  //   Rising Edge Triggered D Flip Flop
endmodule
