// Logisim project SequentialMultipler.circ as structural Verilog: 4 circuits, main circuit Multiplier
module Multiplier (
  input  [3:0] A,
  input  RESET,
  input  [3:0] B,
  output DONE,
  output [7:0] PRODUCT
);

  wire ain_1_toaddornottoadd, and_1_out, and_2_out, clock_1_out, not_1_out, not_2_out, or_1_out;
  wire [3:0] ain_1_out_6;
  wire [7:0] bin_1_bout, multiplexer_1_out;

  // Probe on A
  not not_1 (not_1_out, RESET);
  and and_1 (and_1_out, and_2_out, not_2_out);
  and and_2 (and_2_out, not_1_out, clock_1_out);
  Clock clock_1 (.out(clock_1_out));
  Counter #(.width(1), .max('h1), .ongoal("load")) counter_1 (
    .clr(RESET), .up(1'b1), .clk(and_1_out), .D(1'b0), .carry(DONE));  // open: load, count, Q
  not not_2 (not_2_out, DONE);
  aIn ain_1 (
    .Load(RESET), .Shift(1'b1), .Clock(clock_1_out), .A(A), .ToAddorNottoAdd(ain_1_toaddornottoadd),
    .out_6(ain_1_out_6));
  // Probe on ain_1_out_6
  // Probe on B
  Multiplexer #(.width(8)) multiplexer_1 (
    .in1(bin_1_bout), .out(multiplexer_1_out), .sel(or_1_out), .en(ain_1_toaddornottoadd));  // open: in0
  BIn bin_1 (.Load(RESET), .Shift(1'b1), .Clock(clock_1_out), .B(B), .Bout(bin_1_bout));
  // Probe on bin_1_bout
  or or_1 (or_1_out, RESET, clock_1_out);
  MagicHappensHere magichappenshere_1 (.toAdd(multiplexer_1_out), .clock(or_1_out), .Reset(RESET), .Outtot(PRODUCT));
  // Probe on PRODUCT

  // Notes on the sheet:
  //   Alisa GAGINA 260770497
endmodule

module aIn (
  input  Load,
  input  Shift,
  input  Clock,
  input  [3:0] A,
  output ToAddorNottoAdd,
  output [3:0] out_6
);

  // Shift_Register #(.length(4)) shift_register_1: pin names not known; wires that end beside it: Load, Shift, Clock, 1'b0, A[0], A[1], A[2], A[3], out_6[0], out_6[1], out_6[2], out_6[3]

  assign ToAddorNottoAdd = out_6[3];
endmodule

module BIn (
  input  Load,
  input  Shift,
  input  Clock,
  input  [3:0] B,
  output [7:0] Bout
);

  wire [7:0] bit_extender_1_out;

  assign bit_extender_1_out = {{4{B[3]}}, B};  // Bit_Extender bit_extender_1
  // Shift_Register shift_register_1: pin names not known; wires that end beside it: Load, Shift, Clock, 1'b0, bit_extender_1_out[0], bit_extender_1_out[1], bit_extender_1_out[2], bit_extender_1_out[3], bit_extender_1_out[4], bit_extender_1_out[5], bit_extender_1_out[6], bit_extender_1_out[7], Bout[0], Bout[1], Bout[2], Bout[3], Bout[4], Bout[5], Bout[6], Bout[7]
endmodule

module MagicHappensHere (
  input  [7:0] toAdd,
  input  clock,
  input  Reset,
  output [7:0] Outtot
);

  wire adder_1_cout, register_1_q;
  wire [7:0] adder_1_out, register_2_q;

  // Probe on register_2_q
  Adder adder_1 (.a(toAdd), .b(register_2_q), .out(adder_1_out), .cin(register_1_q), .cout(adder_1_cout));
  Register #(.width(1)) register_1 (.D(adder_1_cout), .clk(clock), .Q(register_1_q), .clr(clock));  // open: en
  Multiplexer #(.width(8), .enable("false")) multiplexer_1 (
    .in0(register_2_q), .in1(adder_1_out), .out(Outtot), .sel(clock));
  Register #(.trigger("falling")) register_2 (.D(Outtot), .clk(clock), .Q(register_2_q), .clr(Reset));  // open: en
endmodule
