// Logisim project SequentialMultiplierlan.circ as structural Verilog: 1 circuit, main circuit Multiplier
module Multiplier (
  input  [7:0] A,
  input  [7:0] B,
  input  START,
  output [15:0] PRODUCT,
  output DONE
);


  // Notes on the sheet:
  //   First name LAST NAME, Student Number
endmodule
