// Logisim project SevenSegDec.circ as structural Verilog: 1 circuit, main circuit SevenSegDec
module SevenSegDec (
  input  A3,
  input  A2,
  input  A1,
  input  A0,
  output S0,
  output S1,
  output S2,
  output S3,
  output S4,
  output S5,
  output S6
);

  wire and_1_out, and_2_out, and_3_out, and_4_out, and_5_out, and_6_out, and_7_out, and_8_out, and_9_out,
       and_10_out, and_12_out, and_13_out, and_14_out, and_15_out, and_16_out, and_17_out, not_1_out,
       not_2_out, not_3_out, not_4_out, or_2_out;

  not not_1 (not_1_out, A3);
  not not_2 (not_2_out, A2);
  not not_3 (not_3_out, A1);
  not not_4 (not_4_out, A0);
  and and_1 (and_1_out, A0, not_3_out, not_2_out, A3);
  or or_1 (S4, A0, not_3_out, not_2_out, A3);
  and and_2 (and_2_out, not_1_out, not_2_out, not_3_out, A0);
  and and_3 (and_3_out, A2, not_3_out);
  and and_4 (and_4_out, not_2_out, A1);
  and and_5 (and_5_out, A2, not_4_out);
  and and_6 (and_6_out, not_2_out, A1, not_4_out);
  and and_7 (and_7_out, not_1_out, not_3_out);
  or or_2 (or_2_out, and_3_out, not_4_out);
  and and_8 (and_8_out, A3, not_2_out, not_3_out, A0);
  and and_9 (and_9_out, not_1_out, not_2_out, A1, A0);
  or or_3 (S5, and_4_out, and_5_out, and_2_out, and_1_out);
  nor nor_1 (S0, A3, and_6_out);
  and and_10 (and_10_out, A3, A1);
  and and_11 (S2, not_1_out, or_2_out);
  and and_12 (and_12_out, not_1_out, A2, A1, not_4_out);
  and and_13 (and_13_out, not_1_out, not_2_out, not_3_out, not_4_out);
  and and_14 (and_14_out, not_3_out, not_2_out, not_1_out);
  and and_15 (and_15_out, A1, A0);
  and and_16 (and_16_out, A0, A3);
  or or_4 (S1, and_10_out, not_4_out, A2, and_7_out);
  or or_5 (S3, and_8_out, and_12_out, and_9_out, and_13_out);
  or or_6 (S6, and_14_out, and_15_out, and_16_out, and_17_out);
  and and_17 (and_17_out, not_4_out, A1, A2, not_1_out);
  _7_Segment_Display u_7_segment_display_1 (.g(S0), .f(S1), .a(S2), .b(S3), .e(S4), .d(S5), .c(S6));  // open: dp

  // Notes on the sheet:
  //   A3 
  //   A3'
  //   A2
  //   A2'
  //   A1
  //   A1'
  //   A0
  //   A0'
  //   Alisa Gagina 260770497
  //   A3+A2'+A1'+A0
  //   these two are part of the s5 gate
  //   (A3+A2'A1A0')'
  //   A3A1+A3'A1'+A2+A0'
  //   A3'(A0'+A2A1')
  //   A2A0'+A2'A1+A3'A2'A1'A0+A3A2'A1'A0
  //   A3A2'A1'A0+A3'A2A1A0'+A3'A2'A1A0+A3'A2'A1'A0'
  //   A3'A2'A1'+A1A0+A3A0+A3'A2A1A0'
endmodule
